# Fritzing sketch Design (saved by Fritzing 0.9.3b)
circuit board: 8.46667cm x 5.64444cm
breadboards: 1

parts:
  Part1 = Arduino Uno (Rev3)
  T1 = LM35 Temperature Sensor [package="TO92 [THT]"]
  LED1 = LED - 5mm [color="Red (633nm)" package="5 mm [THT]"]
  LED2 = LED - 5mm [color="Yellow (595nm)" package="5 mm [THT]"]
  IR1 = TSOP312.., 314.. [package=THT]
  R1 = Resistor [tolerance=±5% resistance=220 package=THT]
  R2 = Resistor [tolerance=±5% resistance=220 package=THT]

nets:
  N1: Part1.A0, T1.Vout
  N2: Part1.D11_PWM/MOSI, IR1.Data
  N3: Part1.D12/MISO, R1.Pin_1
  N4: Part1.D13/SCK, R2.Pin_1
  GND: Part1.GND, T1.GND, LED1.cathode, LED2.cathode, IR1.GND
  N5: Part1.5V, T1.+Vs, IR1.Vs
  N6: LED1.anode, R1.Pin_0
  N7: LED2.anode, R2.Pin_0

// code stored in the sketch: Air_Conditioner.ino

